# Fritzing sketch lab7 (saved by Fritzing 0.9.3b)
breadboards: 1

parts:
  Raspberry_Pi_1 = Raspberry Pi 3 [part_number=RPI-3-V1.2]
  U1 = LCD-16X2 [package=lcd-16x2]
  S1 = Pushbutton [package="[SMD]"]
  R1 = Rotary Potentiometer (Small) [maximum_resistance=100kΩ package=THT]

nets:
  N1: Raspberry_Pi_1.GIPO17, U1.DB4
  N2: Raspberry_Pi_1.GIPO27, U1.DB6
  N3: Raspberry_Pi_1.GIPO22, U1.DB7
  N4: Raspberry_Pi_1.GIPO19, S1.Pin_1, S1.Pin_2
  N5: Raspberry_Pi_1.GIPO24, U1.RS
  N6: Raspberry_Pi_1.GIPO23, U1.E
  N7: Raspberry_Pi_1.GIPO18, U1.DB5
  GND: Raspberry_Pi_1.GND, U1.VSS, U1.R_W, U1.K, S1.Pin_3, S1.Pin_4, R1.leg1
  5V: Raspberry_Pi_1.5V, U1.VDD, U1.A, R1.leg2
  N8: U1.VO, R1.wiper
